# Fritzing sketch smartdrinks-schematics (saved by Fritzing 0.9.10b)
breadboards: 1

parts:
  M1 = RioRand LM2596
  Mod1 = Amica NodeMCU DEVKIT 1.0
  Mod2 = generic-ac-power-supply [package=THT]
  S1 = H-Bridge with L298N
  S2 = H-Bridge with L298N
  M2 = DC Motor [voltage_(max)=12V voltage_(min)=3V]
  M3 = DC Motor [voltage_(max)=12V voltage_(min)=3V]
  M4 = DC Motor [voltage_(max)=12V voltage_(min)=3V]
  M5 = DC Motor [voltage_(max)=12V voltage_(min)=3V]
  HC-SR04_Sensor_1 = HC-SR04 Ultrasonic Distance Sensor

nets:
  12V: M1.Pin_1, Mod2.pin3#2, S1.12V, S2.12V
  N1: M1.Pin_2, Mod2.pin3#3
  N2: M1.Pin_3, Mod1.pin_30, HC-SR04_Sensor_1.VCC
  GND: M1.Pin_4, Mod1.pin2, Mod1.pin_9, Mod1.pin_25, Mod1.pin_29, S1.GND, S2.GND, HC-SR04_Sensor_1.GND
  N3: Mod1.pin1, Mod1.pin_10, Mod1.pin_26
  N4: Mod1.pin5, HC-SR04_Sensor_1.ECHO
  N5: Mod1.pin6, HC-SR04_Sensor_1.TRIG
  N6: Mod1.pin7, S2.IN3
  N7: Mod1.pin8, S2.IN1
  N8: Mod1.pin_12, S1.IN3
  N9: Mod1.pin_13, S1.IN1
  N10: Mod1.pin_14, S1.ENA, S1.ENB, S2.ENA, S2.ENB
  N11: S1.M1-01, M3.pin_1
  N12: S1.M1-02, M3.pin_2
  N13: S1.M2-01, M2.pin_2
  N14: S1.M2-02, M2.pin_1
  N15: S2.M1-01, M4.pin_1
  N16: S2.M1-02, M4.pin_2
  N17: S2.M2-01, M5.pin_2
  N18: S2.M2-02, M5.pin_1

custom parts:
  generic-ac-power-supply: Generic ac power supply module. Use as is, or customize the svgs to fit your particular device (as they are all different.) Provides AC input and single DC output. PCB is generic and will need modifications if you intend to do a pcb mount.
  H-Bridge with L298N: h-bridge
